// Logisim project PPUPlayer.circ as structural Verilog: 6 circuits, main circuit PPUPlayer_main
module PPUPlayer_main (
);

  wire CLK_out, n2c02_ntsc_1_p18, n2c02_ntsc_1_p20, n2c02_ntsc_1_p51, n2c02_ntsc_1_p52, not_1_out,
       nrom_cartridge_1_nvram_cs, ppuplayer_ntsc_1_datasel, ppuplayer_ntsc_1_ndbe, ppuplayer_ntsc_1_r_w,
       ppuplayer_ntsc_1_rs0, ppuplayer_ntsc_1_rs1, ppuplayer_ntsc_1_rs2;
  wire [5:0] n2c02_ntsc_1_p45;
  wire [7:0] ls373_1_val_out, n2c02_ntsc_1_p21, n2c02_ntsc_1_p22, n2c02_ntsc_1_p23, ppuplayer_ntsc_1_db_out;
  wire [10:0] n2c02_ntsc_1_p54;
  wire [10:10] nrom_cartridge_1_vram_a10;
  wire [23:0] ppuplayer_ntsc_1_regaddr;
  wire [31:0] rom_1_data;

  Clock CLK (.out(CLK_out));
  PPUPlayer_NTSC ppuplayer_ntsc_1 (
    .CLK(CLK_out), .RegData(rom_1_data), .R_W(ppuplayer_ntsc_1_r_w), .DB_Out(ppuplayer_ntsc_1_db_out),
    .RS0(ppuplayer_ntsc_1_rs0), .RS1(ppuplayer_ntsc_1_rs1), .RS2(ppuplayer_ntsc_1_rs2),
    .nDBE(ppuplayer_ntsc_1_ndbe), .RegAddr(ppuplayer_ntsc_1_regaddr), .DataSel(ppuplayer_ntsc_1_datasel));
  ROM #(.addrWidth(24), .dataWidth(32)) rom_1 (
    .addr(ppuplayer_ntsc_1_regaddr), .data(rom_1_data), .sel(ppuplayer_ntsc_1_datasel));
  // _2C02_NTSC 2c02_ntsc_1: pin names not known; wires that end beside it: ppuplayer_ntsc_1_r_w, ppuplayer_ntsc_1_db_out[0], ppuplayer_ntsc_1_db_out[1], ppuplayer_ntsc_1_db_out[2], ppuplayer_ntsc_1_db_out[3], ppuplayer_ntsc_1_db_out[4], ppuplayer_ntsc_1_db_out[5], ppuplayer_ntsc_1_db_out[6], ppuplayer_ntsc_1_db_out[7], ppuplayer_ntsc_1_rs0, ppuplayer_ntsc_1_rs1, ppuplayer_ntsc_1_rs2, ppuplayer_ntsc_1_ndbe, 1'b0, 1'b0, 1'b0, 1'b0, n2c02_ntsc_1_p18, CLK_out, n2c02_ntsc_1_p20, n2c02_ntsc_1_p21[0], n2c02_ntsc_1_p22[0], n2c02_ntsc_1_p23[0], n2c02_ntsc_1_p21[1], n2c02_ntsc_1_p22[1], n2c02_ntsc_1_p23[1], n2c02_ntsc_1_p21[2], n2c02_ntsc_1_p22[2], n2c02_ntsc_1_p23[2], n2c02_ntsc_1_p21[3], n2c02_ntsc_1_p22[3], n2c02_ntsc_1_p23[3], n2c02_ntsc_1_p21[4], n2c02_ntsc_1_p22[4], n2c02_ntsc_1_p23[4], n2c02_ntsc_1_p21[5], n2c02_ntsc_1_p22[5], n2c02_ntsc_1_p23[5], n2c02_ntsc_1_p21[6], n2c02_ntsc_1_p22[6], n2c02_ntsc_1_p23[6], n2c02_ntsc_1_p21[7], n2c02_ntsc_1_p22[7], n2c02_ntsc_1_p23[7], n2c02_ntsc_1_p45[0], n2c02_ntsc_1_p45[1], n2c02_ntsc_1_p45[2], n2c02_ntsc_1_p45[3], n2c02_ntsc_1_p45[4], n2c02_ntsc_1_p45[5], n2c02_ntsc_1_p51, n2c02_ntsc_1_p52, 1'b1, n2c02_ntsc_1_p54
  LED led_1 (.in(n2c02_ntsc_1_p18));
  VideoDumper videodumper_1 (.CLK(CLK_out), .VideoIn(n2c02_ntsc_1_p54));
  LS373 ls373_1 (.LE(n2c02_ntsc_1_p20), .nOE(1'b0), .val_in(n2c02_ntsc_1_p21), .val_out(ls373_1_val_out));
  NROM_Cartridge nrom_cartridge_1 (
    .PPUData_In(n2c02_ntsc_1_p22), .nRD(n2c02_ntsc_1_p51), .nWR(n2c02_ntsc_1_p52),
    .PPUAddr({n2c02_ntsc_1_p45, ls373_1_val_out}), .nPA13(not_1_out), .PPUData_Out(n2c02_ntsc_1_p23),
    .nVRAM_CS(nrom_cartridge_1_nvram_cs), .VRAM_A10(nrom_cartridge_1_vram_a10[10]));
  not not_1 (not_1_out, n2c02_ntsc_1_p45[5]);
  SRAM sram_1 (
    .nCS(nrom_cartridge_1_nvram_cs), .nWE(n2c02_ntsc_1_p52), .nOE(n2c02_ntsc_1_p51),
    .Addr({nrom_cartridge_1_vram_a10[10], n2c02_ntsc_1_p45[1:0], ls373_1_val_out}),
    .Data_In(n2c02_ntsc_1_p22), .Data_Out(n2c02_ntsc_1_p23));

  // Notes on the sheet:
  //   RegDump Mem
  //   PA0-7
  //   PPU Data Out
  //   PPU Data In
endmodule

module PPUPlayer_NTSC (
  input  CLK,
  input  [31:0] RegData,
  output R_W,
  output [7:0] DB_Out,
  output RS0,
  output RS1,
  output RS2,
  output nDBE,
  output [23:0] RegAddr,
  output DataSel
);


  // Notes on the sheet:
  //   CPU I/F
endmodule

module SRAM (
  input  nCS,
  input  nWE,
  input  nOE,
  input  [10:0] Addr,
  input  [7:0] Data_In,
  output [7:0] Data_Out
);

  wire not_1_out, not_2_out, not_3_out;

  not not_1 (not_1_out, nCS);
  not not_2 (not_2_out, nWE);
  not not_3 (not_3_out, nOE);
  RAM #(.addrWidth(11), .bus("separate")) ram_1 (
    .addr(Addr), .din(Data_In), .data(Data_Out), .str(not_2_out), .sel(not_1_out), .clk(not_1_out),
    .ld(not_3_out));  // open: clr
endmodule

module LS373 (
  input  LE,
  input  nOE,
  input  [7:0] val_in,
  output [7:0] val_out
);

  wire not_1_out;
  wire [7:0] register_1_q;

  not not_1 (not_1_out, nOE);
  Register #(.trigger("high")) register_1 (.D(val_in), .en(LE), .Q(register_1_q), .clk(LE));  // open: clr
  assign val_out = not_1_out ? register_1_q : 8'bz;  // Controlled_Buffer controlled_buffer_1
endmodule

module NROM_Cartridge (
  input  [7:0] PPUData_In,
  input  nRD,
  input  nWR,
  input  [13:0] PPUAddr,
  input  nPA13,
  output [7:0] PPUData_Out,
  output nVRAM_CS,
  output VRAM_A10
);

  wire not_1_out;

  not not_1 (not_1_out, nRD);
  ROM #(.addrWidth(13)) rom_1 (.addr(PPUAddr[12:0]), .data(PPUData_Out), .sel(not_1_out));

  assign nVRAM_CS = nPA13;
  assign VRAM_A10 = 1'b1;

  // Notes on the sheet:
  //   N.C.
  //   N.C.
  //   N.C.
  //   Simple NROM cartridge (without PRG)
  //   CHR-ROM (0x2000 bytes)
  //   1: V-Mirroring, 0: H-Mirroring
endmodule

module VideoDumper (
  input  CLK,
  input  [10:0] VideoIn
);
endmodule
